# Fritzing sketch final (saved by Fritzing 0.9.3b)
breadboards: 1

parts:
  Part1 = Photon
  Grove1 = Grove OLED 128x96  # not connected
  J1 = Piezo Speaker
  LED1 = smd LED [color="Red (633nm)" package="0603 [SMD]"]
  R1 = Resistor [tolerance=±5% resistance=220 package=THT]

nets:
  N1: Part1.GND, R1.Pin_0
  N2: Part1.D0, LED1.cathode
  N3: Part1.D2, J1.pin2
  N4: LED1.anode, R1.Pin_1

notes:
  Turn light off "button"
  Turn alarm off "button"
  display weather page "button"
  (INPUT_PULLUP)
